# Fritzing sketch tt_hr_network_sensor (saved by Fritzing 0.9.0b)
breadboards: 2

parts:
  Composant1 = Arduino Uno (Rev3) [part_number=Master]
  Raspberry_Pi_B_rev1 = Raspberry Pi B rev1  # not connected
  Composant2 = Arduino Uno (Rev3)
  IC1 = IC, DIP package, 8 pins [chip_label=MAX485]
  IC2 = IC, DIP package, 8 pins [chip_label=MAX485]
  DHT2 = DHT22 Humidity and Temperature Sensor
  Request_recieved_from_Master_LED = LED - 5mm [color="Yellow (585nm)" package="5 mm [THT]"]
  DHT3 = DHT22 Humidity and Temperature Sensor
  RS485_communication_LED = RGB LED - (4 legs) [package="5 mm [THT]"]
  R2 = Resistor [tolerance=±5% resistance=1k package=THT]
  R3 = Resistor [tolerance=±5% resistance=1k package=THT]
  DHT22_reading_status_LED = RGB LED (com. cathode, rgb) [package="5 mm [THT]"]
  R5 = Resistor [tolerance=±5% resistance=4.7k package=THT]
  R7 = Resistor [tolerance=±5% resistance=4.7k package=THT]
  R8 = Resistor [tolerance=±5% resistance=4.7k package=THT]
  R9 = Resistor [tolerance=±5% resistance=4.7k package=THT]
  R10 = Resistor [tolerance=±5% resistance=4.7k package=THT]
  R11 = Resistor [tolerance=±5% resistance=4.7k package=THT]
  R12 = Resistor [tolerance=±5% resistance=330 package=THT]
  RS485_communication_LED1 = RGB LED - (4 legs) [package="5 mm [THT]"]
  R13 = Resistor [tolerance=±5% resistance=4.7k package=THT]
  R14 = Resistor [tolerance=±5% resistance=4.7k package=THT]
  R15 = Resistor [tolerance=±5% resistance=4.7k package=THT]
  R16 = Resistor [tolerance=±5% resistance=240 package=THT]

nets:
  N1: Composant1.D8, R15.Pin_0
  N2: Composant1.D9_PWM, R14.Pin_0
  N3: Composant1.D10_PWM/SS, R13.Pin_0
  N4: Composant1.D11_PWM/MOSI, DHT3.DATA, R3.Pin_0
  GND: Composant1.GND, DHT3.GND
  N5: Composant1.D2, IC1.pin1
  N6: Composant1.D3_PWM, IC1.pin4
  N7: Composant1.D4, IC1.pin2, IC1.pin3
  N8: Composant1.D5_PWM, R11.Pin_0
  N9: Composant1.D6_PWM, R9.Pin_0
  N10: Composant1.D7, R10.Pin_0
  5V: Composant1.5V, DHT3.VDD, R3.Pin_1
  N11: Composant2.D8, R12.Pin_0
  N12: Composant2.D10_PWM/SS, DHT2.DATA, R2.Pin_0
  GND_2: Composant2.GND, DHT2.GND, Request_recieved_from_Master_LED.cathode
  N13: Composant2.D2, IC2.pin1
  N14: Composant2.D3_PWM, IC2.pin4
  N15: Composant2.D4, IC2.pin2, IC2.pin3
  N16: Composant2.D5_PWM, R7.Pin_0
  N17: Composant2.D6_PWM, R8.Pin_0
  N18: Composant2.D7, R5.Pin_0
  5V_2: Composant2.5V, DHT2.VDD, R2.Pin_1
  N19: IC1.pin5, IC1.pin8
  N20: IC1.pin6, IC2.pin6, R16.Pin_1
  N21: IC1.pin7, IC2.pin7, R16.Pin_0
  N22: Request_recieved_from_Master_LED.anode, R12.Pin_1
  N23: RS485_communication_LED.red_cathode, R10.Pin_1
  N24: RS485_communication_LED.common_anode, R9.Pin_1
  N25: RS485_communication_LED.blue_cathode, R11.Pin_1
  N26: DHT22_reading_status_LED.red_anode, R5.Pin_1
  N27: DHT22_reading_status_LED.common_cathode, R8.Pin_1
  N28: DHT22_reading_status_LED.blue_anode, R7.Pin_1
  N29: RS485_communication_LED1.red_cathode, R13.Pin_1
  N30: RS485_communication_LED1.common_anode, R14.Pin_1
  N31: RS485_communication_LED1.blue_cathode, R15.Pin_1

notes:
  Master
  Slave 1
  USB cable
  Twisted pairs that can run for 1200m
  tt_hr_sensor_network
  iMeteo.ca
